# Fritzing sketch diagram (saved by Fritzing 0.7.7b)
breadboards: 1

parts:
  Arduino1 = Arduino
  LED1 = LED - 5mm [color="Red (633nm)" package="5 mm [THT]"]
  LED2 = LED - 5mm [color="Yellow (592nm)" package="5 mm [THT]"]
  LED3 = LED - 5mm [color="Green (565nm)" package="5 mm [THT]"]
  LED4 = LED - 5mm [color="Blue (505nm)" package="5 mm [THT]"]
  S1 = Pushbutton [package=THT]
  S2 = Pushbutton [package=THT]
  S3 = Pushbutton [package=THT]
  S4 = Pushbutton [package=THT]
  LCD1 = LCD screen
  R1 = Resistor [tolerance=±5% resistance=330 package=THT]
  R2 = Resistor [tolerance=±5% resistance=330 package=THT]
  R3 = Resistor [tolerance=±5% resistance=330 package=THT]
  R4 = Resistor [tolerance=±5% resistance=330 package=THT]
  J1 = Piezo Speaker
  R5 = Resistor [tolerance=±5% resistance=110 package=THT]

nets:
  GND: Arduino1.GND, S1.leg1, S2.leg1, S3.leg1, S4.leg1, LCD1.VSS, R1.Pin_1, R2.Pin_1, R3.Pin_1, R4.Pin_1, J1.pin2
  N1: Arduino1.D13, LED4.anode
  N2: Arduino1.D12, LED3.anode
  N3: Arduino1.D11, LED2.anode
  N4: Arduino1.D10, LED1.cathode, LED1.anode, R1.Pin_0
  N5: Arduino1.D9, R5.Pin_0
  N6: Arduino1.D8, LCD1.V0
  N7: Arduino1.D5, S4.leg0
  N8: Arduino1.D4, S3.leg0
  N9: Arduino1.D3, S2.leg0
  N10: Arduino1.D2, S1.leg0
  +5V: Arduino1.+5V, LCD1.VDD
  N11: LED2.cathode, R2.Pin_0
  N12: LED3.cathode, R3.Pin_0
  N13: LED4.cathode, R4.Pin_0
  N14: J1.pin1, R5.Pin_1
